# Fritzing sketch Scale Dispenser (saved by Fritzing 0.9.3b)
breadboards: 1

parts:
  J1 = Basic Servo
  Part2 = HX711 Weighing Sensor Module
  RE1 = Rotary Encoder [package=THT]
  S1 = Momentary Switch [package=ksa_sealed_tac_switch]
  S3 = Momentary Switch [package=ksa_sealed_tac_switch]
  Load_Cell1 = Load Cell - Red/white/black/green
  LCD2004-I2C1 = LCD2004-I2C
  Part3 = Arduino Uno (Rev3) - ICSP
  R1 = Resistor [tolerance=±5% resistance=10k package="2512 [SMD]"]
  R2 = Resistor [tolerance=±5% resistance=10k package="2512 [SMD]"]

nets:
  N1: J1.pulse, Part3.D6_PWM
  VCC: Part2.VCC, Part3.3V3
  GND: Part2.GND, LCD2004-I2C1.GND, Part3.GND, R1.Pin_0, R2.Pin_0
  N2: Part2.DO/RX, Part3.D8
  N3: Part2.CK/TX, Part3.D7
  N4: Part2.E+, Load_Cell1.wire1
  N5: Part2.E-, Load_Cell1.wire2
  N6: Part2.A+, Load_Cell1.wire3
  N7: RE1.EncoderPinA, Part3.D10_PWM/SS
  VCC_2: RE1.EncoderPinC, S3.2, LCD2004-I2C1.VCC, Part3.5V
  N8: RE1.EncoderPinB, Part3.D9_PWM
  N9: S1.3, Part3.D12/MISO
  N10: S1.4, R2.Pin_1
  N11: S3.3, Part3.D13/SCK
  N12: S3.4, R1.Pin_1
  N13: LCD2004-I2C1.SDA, Part3.A4/SDA
  N14: LCD2004-I2C1.SCL, Part3.A5/SCL

custom parts:
  Load Cell - Red/white/black/green: A rectangle load cell/weighting pressure Sensor with four wires - Red, white, black, green. Normally corresponding with E+, E-, A+, A- respectively.
  LCD2004-I2C: A standard character display with 4x20 characters. Comes in many colors with LCM2004 IIC attached.

// code stored in the sketch: Scale_Dispenser.ino

#include "HX711.h"
#include <Servo.h>
#include <Rotary.h>
#include <Wire.h> 
#include <LiquidCrystal_I2C.h>

HX711 scale(6, 7);
Rotary rotary = Rotary(10,11);
LiquidCrystal_I2C lcd(0x27, 16, 2);
Servo servo;
//Buttons
int toggleBtn = 2;
int enterBtn = 5;

//Servo
float servoPin = 9;
//Scale values
float calFactor = -359.50;
float value = 0;
float valueTo = 0;

volatile int openPos = 60;
volatile int closePos = 0;
volatile bool allRun = false;

void setup() {
  lcd.begin();
  lcd.backlight();
  lcd.setCursor(0,0);
  lcd.println("Scale Starting");   
  
  allRun = false;
  //attach servo controls
  servo.attach(servoPin);
  servo.write(closePos);

  //start scale and tare
  scale.set_scale();
  scale.tare();  //Reset the scale to 0
  
//btn setup
pinMode(toggleBtn, INPUT);
pinMode(enterBtn, INPUT);
attachInterrupt(digitalPinToInterrupt(toggleBtn), toggle, CHANGE); 
  lcd.setCursor(0,0);
  lcd.println("Scale Ready");
  delay(500); 
  updateMessageToUser();
}
void loop() {
  
unsigned char result = rotary.process();
  if (result == DIR_CW) {
    valueTo++;
    updateMessageToUser();
  } else if (result == DIR_CCW && valueTo >= 1) {
    valueTo = valueTo - 0.10;
    updateMessageToUser();
  }
  
  int btnState = digitalRead(enterBtn);
  
if(btnState == HIGH){
  static unsigned long lstTime = 0;
  unsigned long thisTime = millis();
  if(thisTime - lstTime > 250) {
      lcd.setCursor(0,0);
      lcd.println("Enter button pressed");
      while(value < (valueTo)) {    
        servo.write(openPos);
        allRun = true;
        weigh();     
        }
      servo.write(closePos); 
  }
  lstTime = thisTime;
}

}
void weigh() {
    scale.set_scale(calFactor);
    if(scale.get_units(1) < 0) {
     value = 0; 
      }
      else {
        value = scale.get_units(1);
        }
        updateMessageToUser();
  }
void toggle(){
  static unsigned long lstTime = 0;
  unsigned long itrTime = millis();
  if(itrTime - lstTime > 250) {
      lcd.setCursor(0,0);
      lcd.println("Toggle button pressed");
  if(allRun == false) {
    valueTo = 999;
    servo.write(openPos);
    allRun = true;
    }
    else {
      valueTo = 0;
      servo.write(closePos);
      allRun = false;
      }
      updateMessageToUser();
      
    }
  lstTime = itrTime;
}
void updateMessageToUser() {
      lcd.setCursor(0,0);
      lcd.println();
    if(valueTo == 999) {
      lcd.print("Override");     
    }
    else {
      lcd.print(valueTo);  
    }  
      lcd.print("===");
      lcd.print(value);
}
